# Fritzing sketch schematic (saved by Fritzing 0.9.3b)
breadboards: 1

parts:
  part = DC Power [voltage=12V]
  U1 = attiny85 [package=dip]
  MOSFET = Basic FET N-Channel [package="TO220 [THT]"]
  LED1 = LEDs [package=led10mm]
  Brightness_Pot = POT [package=pot_mammoth]
  LDR = Photocell (LDR) [package=THT]
  MC7805CT = Voltage Regulator - 5V [package="DPak [SMD]"]
  1000uF_16v = Capacitor Polarized [package=panasonic_e]
  part_2 = Resistor [tolerance=±5% resistance=10k package=THT]
  part_3 = Resistor [tolerance=±5% resistance=10k package=THT]
  Threshold_Pot = POT [package=pot_mammoth]

nets:
  N1: part.V+, LED1.C, MC7805CT.input_voltage
  N2: part.V-, MOSFET.source, Brightness_Pot.E, MC7805CT.GND, 1000uF_16v.-, part_2.Pin_0, Threshold_Pot.E
  N3: U1.Pin_2, Threshold_Pot.S
  N4: U1.Pin_3, Brightness_Pot.S
  N5: U1.Pin_4, part_3.Pin_0
  N6: U1.Pin_5, MOSFET.gate, part_2.Pin_1
  N7: U1.Pin_7, LDR.pin_1, part_3.Pin_1
  N8: U1.Pin_8, Brightness_Pot.A, LDR.pin_0, MC7805CT.output_voltage, 1000uF_16v.+, Threshold_Pot.A
  N9: MOSFET.drain, LED1.A
